// Logisim project mips.circ as structural Verilog: 4 circuits, main circuit main
module main (
);

  wire ALU_zero, and_1_out, and_2_out, and_3_out, and_4_out, and_5_out, and_6_out, clock_1_out,
       Control_alusrc, Control_branch, Control_branchne, Control_memread, Control_memtoreg, Control_memwrite,
       Control_regdst, Control_regwrite, demultiplexer_2_out8, demultiplexer_2_out9, demultiplexer_2_out10,
       demultiplexer_2_out16, jal_out, not_1_out, not_2_out, not_3_out, not_4_out, not_5_out, not_6_out,
       not_7_out, not_8_out, not_9_out, not_10_out, not_11_out, not_12_out, not_13_out, not_14_out,
       not_15_out, not_16_out, or_1_out, or_2_out, or_3_out, Reset_PC_out;
  wire [3:0] Control_aluop;
  wire [4:0] multiplexer_5_out;
  wire [5:0] ram_1_data_2;
  wire [23:0] adder_1_out, adder_2_out, multiplexer_1_out, multiplexer_2_out, multiplexer_3_out,
       multiplexer_4_out, pc_q;
  wire [25:0] ram_1_data;
  wire [31:0] ALU_output, demultiplexer_1_out8, demultiplexer_1_out9, demultiplexer_1_out10,
       demultiplexer_1_out16, multiplexer_6_out, multiplexer_7_out, multiplexer_8_out, ra_q, ram_2_data,
       s0_q, Sign_Extend__32bit, t0_q, t1_q, t2_q, zero_q;
  wire [31:24] multiplexer_4_out_2;

  Button Reset_PC (.out(Reset_PC_out));
  not not_1 (not_1_out, ram_1_data[4]);
  not not_2 (not_2_out, ram_1_data[1]);
  not not_3 (not_3_out, ram_1_data[5]);
  not not_4 (not_4_out, ram_1_data[0]);
  not not_5 (not_5_out, ram_1_data[2]);
  and and_1 (and_1_out, not_3_out, not_1_out, ram_1_data[3], not_5_out, not_2_out, not_4_out);
  Register #(.width(24)) pc (.D(multiplexer_3_out), .Q(pc_q), .clk(clock_1_out), .clr(Reset_PC_out));  // open: en
  Clock clock_1 (.out(clock_1_out));
  not not_6 (not_6_out, ram_1_data_2[5]);
  not not_7 (not_7_out, ram_1_data_2[3]);
  not not_8 (not_8_out, ram_1_data_2[1]);
  not not_9 (not_9_out, ram_1_data_2[0]);
  not not_10 (not_10_out, ram_1_data_2[2]);
  not not_11 (not_11_out, ram_1_data_2[4]);
  and and_2 (and_2_out, not_6_out, not_11_out, not_7_out, not_10_out, not_8_out, not_9_out);
  Adder #(.width(24)) adder_1 (.a(24'h1), .b(pc_q), .out(adder_1_out));  // open: cin, cout
  Multiplexer #(.width(24), .enable("false")) multiplexer_1 (
    .in0(ram_1_data[23:0]), .in1(multiplexer_4_out), .out(multiplexer_1_out), .sel(and_3_out));
  and and_3 (and_3_out, and_2_out, and_1_out);
  Multiplexer #(.width(24), .enable("false")) multiplexer_2 (
    .in0(adder_1_out), .in1(adder_2_out), .out(multiplexer_2_out), .sel(or_1_out));
  or or_1 (or_1_out, and_4_out, and_5_out);
  Adder #(.width(24)) adder_2 (.a(adder_1_out), .b(Sign_Extend__32bit[23:0]), .out(adder_2_out));  // open: cin, cout
  and jal (jal_out, and_6_out, ram_1_data_2[0]);
  or or_2 (or_2_out, and_3_out, and_6_out);
  Register #(.width(32)) s0 (
    .D(demultiplexer_1_out16), .en(demultiplexer_2_out16), .Q(s0_q), .clk(clock_1_out), .clr(Reset_PC_out));
  Register #(.width(32)) ra (
    .D({{8{1'b0}}, adder_1_out}), .en(jal_out), .Q(ra_q), .clk(clock_1_out), .clr(Reset_PC_out));
  Multiplexer #(.width(24), .enable("false")) multiplexer_3 (
    .in0(multiplexer_2_out), .in1(multiplexer_1_out), .out(multiplexer_3_out), .sel(or_2_out));
  and and_4 (and_4_out, not_12_out, Control_branchne);
  and and_5 (and_5_out, Control_branch, ALU_zero);
  not not_12 (not_12_out, ALU_zero);
  RAM #(.addrWidth(24), .dataWidth(32)) ram_1 (
    .addr(pc_q), .data({ram_1_data_2, ram_1_data}), .clk(clock_1_out));  // open: sel, ld, clr
  Control_Unit Control (
    .Instruction({ram_1_data_2, ram_1_data}), .RegDst(Control_regdst), .Branch(Control_branch),
    .MemRead(Control_memread), .MemtoReg(Control_memtoreg), .MemWrite(Control_memwrite),
    .ALUSrc(Control_alusrc), .RegWrite(Control_regwrite), .BranchNe(Control_branchne), .ALUOp(Control_aluop));
  not not_13 (not_13_out, ram_1_data_2[5]);
  Sign_Extend Sign_Extend (._16bit(ram_1_data[15:0]), ._32bit(Sign_Extend__32bit));
  not not_14 (not_14_out, ram_1_data_2[2]);
  not not_15 (not_15_out, ram_1_data_2[3]);
  not not_16 (not_16_out, ram_1_data_2[4]);
  Register #(.width(32)) zero (.Q(zero_q), .clk(clock_1_out), .clr(Reset_PC_out));  // open: D, en
  Register #(.width(32)) t0 (
    .D(demultiplexer_1_out8), .en(demultiplexer_2_out8), .Q(t0_q), .clk(clock_1_out), .clr(Reset_PC_out));
  Register #(.width(32)) t1 (
    .D(demultiplexer_1_out9), .en(demultiplexer_2_out9), .Q(t1_q), .clk(clock_1_out), .clr(Reset_PC_out));
  Register #(.width(32)) t2 (
    .D(demultiplexer_1_out10), .en(demultiplexer_2_out10), .Q(t2_q), .clk(clock_1_out), .clr(Reset_PC_out));
  Multiplexer #(.select(5), .width(32), .enable("false")) multiplexer_4 (
    .in0(zero_q), .in8(t0_q), .in9(t1_q), .in10(t2_q), .in16(s0_q), .in31(ra_q),
    .out({multiplexer_4_out_2, multiplexer_4_out}), .sel(ram_1_data[25:21]));  // open: in1, in2, in3, in4, in5, in6, in7, in11, in12, in13, in14, in15, in17, in18, in19, in20, in21, in22, in23, in24, in25, in26, in27, in28, in29, in30
  Multiplexer #(.width(5)) multiplexer_5 (
    .in0(ram_1_data[20:16]), .in1(ram_1_data[15:11]), .out(multiplexer_5_out), .sel(Control_regdst),
    .en(Control_regwrite));
  and and_6 (and_6_out, ram_1_data_2[1], not_14_out, not_15_out, not_16_out, not_13_out);
  Multiplexer #(.select(5), .width(32), .enable("false")) multiplexer_6 (
    .in0(zero_q), .in8(t0_q), .in9(t1_q), .in10(t2_q), .in16(s0_q), .in31(ra_q), .out(multiplexer_6_out),
    .sel(ram_1_data[20:16]));  // open: in1, in2, in3, in4, in5, in6, in7, in11, in12, in13, in14, in15, in17, in18, in19, in20, in21, in22, in23, in24, in25, in26, in27, in28, in29, in30
  Multiplexer #(.width(32), .enable("false")) multiplexer_7 (
    .in0(multiplexer_6_out), .in1(Sign_Extend__32bit), .out(multiplexer_7_out), .sel(Control_alusrc));
  ALU ALU (
    .rs({multiplexer_4_out_2, multiplexer_4_out}), .rt___I(multiplexer_7_out), .shamt(ram_1_data[10:6]),
    .ALU_op(Control_aluop), .Output(ALU_output), .zero(ALU_zero));  // open: less_than
  Demultiplexer #(.select(5), .width(32)) demultiplexer_1 (
    .out8(demultiplexer_1_out8), .out9(demultiplexer_1_out9), .out10(demultiplexer_1_out10),
    .out16(demultiplexer_1_out16), .in(multiplexer_8_out), .sel(multiplexer_5_out), .en(Control_regwrite));  // open: out0, out1, out2, out3, out4, out5, out6, out7, out11, out12, out13, out14, out15, out17, out18, out19, out20, out21, out22, out23, out24, out25, out26, out27, out28, out29, out30, out31
  Demultiplexer #(.select(5)) demultiplexer_2 (
    .out8(demultiplexer_2_out8), .out9(demultiplexer_2_out9), .out10(demultiplexer_2_out10),
    .out16(demultiplexer_2_out16), .in(Control_regwrite), .sel(multiplexer_5_out), .en(Control_regwrite));  // open: out0, out1, out2, out3, out4, out5, out6, out7, out11, out12, out13, out14, out15, out17, out18, out19, out20, out21, out22, out23, out24, out25, out26, out27, out28, out29, out30, out31
  or or_3 (or_3_out, Control_memwrite, Control_memread);
  RAM #(.addrWidth(24), .dataWidth(32), .bus("separate")) ram_2 (
    .addr(ALU_output[23:0]), .din(multiplexer_6_out), .data(ram_2_data), .str(Control_memwrite),
    .sel(or_3_out), .clk(clock_1_out), .ld(Control_memread));  // open: clr
  Multiplexer #(.width(32), .enable("false")) multiplexer_8 (
    .in0(ALU_output), .in1(ram_2_data), .out(multiplexer_8_out), .sel(Control_memtoreg));

  // Notes on the sheet:
  //   is jump register?
  //   is R inst?
  //   0 - jump
  //   absolute jump:
  //   1 - jump register
  //   R
  //   I
  //   J
  //   true - if jump OR jump and link
  //   rs
  //   Rt or Rd (for Dst)
  //   rt
endmodule

module ALU (
  input  [31:0] rs,
  input  [31:0] rt___I,
  input  [4:0] shamt,
  input  [3:0] ALU_op,
  output [31:0] Output,
  output zero,
  output less_than
);

  wire [31:0] adder_1_out, and_1_out, nor_1_out, or_1_out, shifter_1_out, shifter_2_out, subtractor_1_out;

  assign and_1_out = rs & rt___I;  // AND_Gate and_1, 32 bits wide
  assign or_1_out = rs | rt___I;  // OR_Gate or_1, 32 bits wide
  Adder #(.width(32)) adder_1 (.a(rs), .b(rt___I), .out(adder_1_out));  // open: cin, cout
  assign nor_1_out = ~(rs | rt___I);  // NOR_Gate nor_1, 32 bits wide
  Subtractor #(.width(32)) subtractor_1 (.a(rs), .b(rt___I), .out(subtractor_1_out));  // open: bin, bout
  Shifter #(.width(32)) shifter_1 (.in(rt___I), .\dist (shamt), .out(shifter_1_out));
  Shifter #(.width(32), .shift("lr")) shifter_2 (.in(rt___I), .\dist (shamt), .out(shifter_2_out));
  Multiplexer #(.select(4), .width(32), .enable("false")) multiplexer_1 (
    .in0(and_1_out), .in1(or_1_out), .in2(adder_1_out), .in3(nor_1_out), .in6(subtractor_1_out),
    .in14(shifter_1_out), .in15(shifter_2_out), .out(Output), .sel(ALU_op));  // open: in4, in5, in7, in8, in9, in10, in11, in12, in13
  Comparator #(.width(32)) comparator_1 (.a(subtractor_1_out), .b({32{1'b0}}), .eq(zero), .lt(less_than));  // open: gt

  // Notes on the sheet:
  //   0000 - and
  //   0001 - or
  //   0010 - add
  //   0011 - nor?
  //   0100 - ??
  //   0101 - ??
  //   0110 - sub
  //   1110 - sll
  //   1111 - srl
  //   0111 - set-on-less-than
endmodule

module Control_Unit (
  input  [31:0] Instruction,
  output RegDst,
  output Branch,
  output MemRead,
  output MemtoReg,
  output MemWrite,
  output ALUSrc,
  output RegWrite,
  output BranchNe,
  output [3:0] ALUOp
);

  wire or_1_out;
  wire [3:0] rom_3_data, rom_4_data;
  wire [7:0] rom_1_data, rom_2_data;

  or or_1 (or_1_out, Instruction[26], Instruction[27], Instruction[28], Instruction[29], Instruction[30], Instruction[31]);
  ROM #(.addrWidth(6)) rom_1 (.addr(Instruction[5:0]), .data(rom_1_data));  // open: sel
  Multiplexer #(.width(8), .enable("false")) multiplexer_1 (
    .in0(rom_1_data), .in1(rom_2_data),
    .out({BranchNe, RegWrite, ALUSrc, MemWrite, MemtoReg, MemRead, Branch, RegDst}), .sel(or_1_out));
  ROM #(.addrWidth(6)) rom_2 (.addr(Instruction[31:26]), .data(rom_2_data));  // open: sel
  ROM #(.addrWidth(6), .dataWidth(4)) rom_3 (.addr(Instruction[5:0]), .data(rom_3_data));  // open: sel
  ROM #(.addrWidth(6), .dataWidth(4)) rom_4 (.addr(Instruction[31:26]), .data(rom_4_data));  // open: sel
  Multiplexer #(.width(4), .enable("false")) multiplexer_2 (
    .in0(rom_3_data), .in1(rom_4_data), .out(ALUOp), .sel(or_1_out));

  // Notes on the sheet:
  //   convert from R function to ALUOp
  //   convert from I function to ALUOp
  //   convert from R function to ALUOp
  //   convert from I opCode to ALUOp
  //   ALUOp
  //   0010 - add
  //   contents of rom_1 (hex, n*v repeats v):
  //   41 0 41 5*0 2 23*0 41 0 41 0 41 41 0 41
  //   contents of rom_2 (hex, n*v repeats v):
  //   4*0 2 80 0 0 60 0 0 60 60 60 21*0 6c 7*0 30
  //   contents of rom_3 (hex, n*v repeats v):
  //   e 0 f 29*0 2 0 6 0 0 1 0 3
  //   contents of rom_4 (hex, n*v repeats v):
  //   4*0 6 6 0 0 2 0 0 1 0 1 21*0 2 7*0 2
  //   0000 - and
  //   0001 - or
  //   0011 - nor?
  //   0100 - ??
  //   0101 - ??
  //   0110 - sub
  //   0111 - set-on-less-than
  //   1100 - ??
  //   1101 - ??
  //   1110 - sll
  //   1111 - srl
  //   RegDst
  //   add R 0x20
  //   addi I 0x8
  //   addiu I 0x9
  //   addu R 0x21
  //   and R 0x24
  //   andi I 0x0c
  //   beq I 0x04
  //   bne I 0x05
  //   j J 0x02
  //   jal J 0x03
  //   jr R 0x08
  //   lbu I 0x24
  //   lhu
  //   ll
  //   lui
  //   lw I 0x23
  //   nor R 0x27
  //   or R 0x25
  //   ori I 0x0d
  //   slt
  //   slti
  //   sltiu
  //   sltu
  //   sll R 0x00
  //   srl R 0x02
  //   sb
  //   sc
  //   sh
  //   sw I 0x2b
  //   sub R 0x22
  //   subu
  //   Branch
  //   MemRead
  //   1             2             4                8                    16             32           64          128
  //   MemWrite
  //   MemtoReg
  //   1             0             0                0                    0                0              1              0          = 0x41
  //   0             0             0                0                    0                1              1              0          = 0x60
  //   0             0             0                0                    0                1              1              0          = 0x60
  //   1             0             0                0                    0                0              1              0          = 0x41
  //   1             0             0                0                    0                0              1              0          = 0x41
  //   0             0             0                0                    0                1              1              0          = 0x60
  //   0             1             0                0                    0                0              0              0          = 0x02
  //   0             0             0                0                    0                0              0              1          = 0x80
  //   0             1             0                0                    0                ?              0              0          = 0x??
  //   0             1             0                0                    0                ?              0              0          = 0x??
  //   0            1             0                0                    0                0              0              0          = 0x02
  //   0             0             1                1                    0                1              1              0          = 0x6c
  //   1             0             0                0                    0                0              1              0          = 0x41
  //   1             0             0                0                    0                0              1              0          = 0x41
  //   0             0             0                0                    0                1              1              0          = 0x60
  //   ALUSrc
  //   1             0             0                0                    0                0              1              0          = 0x41
  //   1             0             0                0                    0                0              1              0          = 0x41
  //   0             0             0                0                    1                1              0              0          = 0x30
  //   1             0             0                0                    0                0              1              0          = 0x41
  //   1             0             0                0                    0                0              1              0          = 0x41
  //   BranchNe
  //   RegWrite
endmodule

module Sign_Extend (
  input  [15:0] _16bit,
  output [31:0] _32bit
);


  assign _32bit = {{17{_16bit[15]}}, _16bit[14:0]};
endmodule
